# Fritzing sketch SPI_Verkabelung IOT2040--TAPAS (saved by Fritzing 0.9.3b)
breadboards: 1

parts:
  IC2 = DIP - 8 pins [chip_label=IC package="DIP (Dual Inline) [THT]"]
  IC1 = TAPAS-Board_V1.0 [chip_label=IC package="DIP (Dual Inline) [THT]"]

nets:
  GND: IC2.GND, IC1.GND
  N1: IC2.PB2/10/SS, IC1.GPIO_53_/_CS_SW1_(1)
  N2: IC2.PB3/11/MOSI, IC1.GPIO_51_/_MDRA
  N3: IC2.PB4/12/MISO, IC1.GPIO_50_/_MDXA
  N4: IC2.PB5/13/SCK, IC1.GPIO52_/_MCLKXA

notes:
  GND
  CLK
  CS
  MISO
  MOSI

custom parts:
  DIP - 8 pins: A DIP stand-in part for whatever IC you want. With 8 pins on a 300mil dual inline package (DIP) footprint.
  TAPAS-Board_V1.0: This is a simplified part to be able to draw fritzing sketches including the TAPAS-Board from Siemens SDI. All the power terminals, the JTAG-Connector and the analog and digital input and output connectors are not prepared for connection yet. This is optional and to be done. Furter there is no pcb footprint designed yet, as the TAPAS-Board will not be soldered to another pcb in the standard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
